# Fritzing sketch server (saved by Fritzing 0.9.4)

parts:
  Raspberry_Pi_1 = Raspberry Pi 3 [part_number=RPI-3-V1.2]
  F2 = Small Fan, based on Fan - Ventilador [package=THT]  # not connected
  Q1 = TRANSISTOR_NPN [part_number=2N2222 package=to-92-ammo]
  R1 = Resistor [tolerance=±5% resistance=680 package=THT]
  D1 = Diode [part_number=diod package=diode-1n4148]  # not connected
  LED1_status = smd LED [color="Red (633nm)" package="0805 [SMD]"]
  R2 = Resistor [tolerance=±5% resistance=680 package=THT]
  OLED2 = 128x32 I2C Monochrome OLED Display
  button_resset = Pushbutton [package="[THT]"]
  Q2_2N2222 = TRANSISTOR_NPN [package=to-92]
  R3 = Resistor [tolerance=±5% resistance=10k package=THT]
  IR_Reciever_(TSOP4838) = IR Reciever
  IR_LED = LEDs [package=led10mm]

nets:
  3V3: Raspberry_Pi_1.3v3, Raspberry_Pi_1.3V3, OLED2.3.3V
  N1: Raspberry_Pi_1.GPIO2, OLED2.SDA
  N2: Raspberry_Pi_1.GPIO3, OLED2.SCL
  GND: Raspberry_Pi_1.GND, Q1.E, R2.Pin_0, OLED2.GND, button_resset.Pin_4, Q2_2N2222.C, IR_Reciever_(TSOP4838).OUT
  N3: Raspberry_Pi_1.GIPO27, IR_Reciever_(TSOP4838).GND
  N4: Raspberry_Pi_1.GIPO22, R3.Pin_1
  N5: Raspberry_Pi_1.GIPO26, button_resset.Pin_2
  N6: Raspberry_Pi_1.GIPO23, R1.Pin_0
  N7: Raspberry_Pi_1.GIPO14, LED1_status.anode
  N8: Q2_2N2222.E, IR_LED.C
  N9: Q2_2N2222.B, R3.Pin_0
  N10: IR_Reciever_(TSOP4838).Vs, IR_LED.A

custom parts:
  Small Fan, based on Fan - Ventilador: Small 2-pin fan, commonly used with single-board computers, 3d-printers, etc. This work is based on a much larger fan, as commonly found in desktop computers
  IR Reciever: Basic infrared reciever
